# Fritzing sketch connections (saved by Fritzing 0.9.3b)

parts:
  ZS-042_RTC1 = ZS-042 RTC Module
  L1 = Solenoid  # not connected
  Part1 = LCD1602-I2C
  S1 = Pushbutton [package="[THT]"]
  S2 = Pushbutton [package="[THT]"]
  S3 = Pushbutton [package="[THT]"]
  S4 = Pushbutton [package="[THT]"]
  S5 = Pushbutton [package="[THT]"]
  S6 = Pushbutton [package="[THT]"]
  Part2 = Arduino Nano (Rev3.0)
  J8 = Power Jack [package=power_jack_smd]  # not connected
  S7 = Square Pushbutton
  VCC1 = Battery block 9V

nets:
  N1: ZS-042_RTC1.SDA#2, Part2.A4
  N2: ZS-042_RTC1.SCL#3, Part2.A5
  N3: ZS-042_RTC1.GND#6, Part1.GND
  N4: ZS-042_RTC1.VCC#7, Part1.VCC
  N5: ZS-042_RTC1.SDA#8, Part1.SDA
  N6: ZS-042_RTC1.SCL#9, Part1.SCL
  N7: S1.Pin_1, Part2.D4
  N8: S1.Pin_3, S1.Pin_4, S2.Pin_3, S2.Pin_4, S3.Pin_3, S3.Pin_4, S4.Pin_3, S4.Pin_4, S5.Pin_3, S5.Pin_4, S6.Pin_3, Part2.GND
  N9: S2.Pin_1, Part2.D5
  N10: S3.Pin_1, Part2.D6
  N11: S4.Pin_1, Part2.D3
  N12: S5.Pin_1, S5.Pin_2, Part2.D2
  N13: S6.Pin_1, Part2.D7
  N14: S7.leg0, VCC1.+

custom parts:
  LCD1602-I2C: A standard character display, usually with 2x16 characters. Comes in many colors with LCM1602 IIC attached.
